# Fritzing sketch OrangePiZeroConnector (saved by Fritzing 0.9.3b)
breadboards: 1

parts:
  J1 = female pin header, 2 pins [form="♀ (female)"]
  OrangePI-13 = female pin header, 13 pins [form="♀ (female)"]
  JLN = female pin header, 3 pins [form="♀ (female)"]
  OrangePI-GPIO = double row female pin header, 26 pins [form="♀ (female)"]
  R1 = Resistor [tolerance=±5% resistance=1k package=THT]
  R2 = Resistor [tolerance=±5% resistance=1k package=THT]
  D1 = Rectifier Diode [part_number=1N4148 package="300 mil [THT]"]
  D2 = Rectifier Diode [part_number=1N4148 package="300 mil [THT]"]
  U1 = 3.5mm Audio Jack [package=audio-jack]

nets:
  5V: J1.pin1, OrangePI-13.pin1, OrangePI-GPIO.pin2
  GND: J1.pin2, OrangePI-13.pin2, JLN.pin1, OrangePI-GPIO.pin6, U1.SLEEVE
  LINEOUTR: OrangePI-13.pin7, U1.RIGHT
  LINEOUTL: OrangePI-13.pin8, U1.LEFT
  LN1: JLN.pin2, R1.Pin_0
  LN2: JLN.pin3, R2.Pin_0
  3V3: OrangePI-GPIO.pin1, D1.cathode, D2.cathode
  GPIO12: OrangePI-GPIO.pin3, R2.Pin_1, D1.anode
  GPIO11: OrangePI-GPIO.pin5, R1.Pin_1, D2.anode
